// Logisim project Logic Diagram 1.circ as structural Verilog: 1 circuit, main circuit main
module main (
);

  wire and_1_out, and_2_out, and_3_out, and_4_out, and_5_out, and_6_out, and_7_out, and_8_out, and_9_out,
       clock_1_out, clock_2_out, clock_3_out, clock_4_out, clock_5_out, clock_6_out, clock_7_out, d_ff_1_q,
       d_ff_2_q, d_ff_3_q, d_ff_4_q, not_1_out, not_2_out, not_3_out, or_1_out, or_2_out, or_3_out, or_4_out,
       or_5_out, or_6_out, or_7_out, undriven, undriven_2, undriven_3, xor_1_out;
  wire [3:0] counter_1_q, counter_2_q, counter_3_q;

  Clock clock_1 (.out(clock_1_out));
  Clock clock_2 (.out(clock_2_out));
  not not_1 (not_1_out, clock_2_out);
  D_Flip_Flop d_ff_1 (
    .clk(not_1_out), .D(and_6_out), .Q(d_ff_1_q), .preset(clock_1_out), .en(1'b1), .reset(or_7_out));  // open: Qn
  not not_2 (not_2_out, d_ff_2_q);
  Counter #(.width(4), .max('hf)) counter_1 (
    .load(not_2_out), .count(1'b1), .Q(counter_1_q), .clk(and_1_out), .clr(and_3_out));  // open: D, carry
  Clock clock_3 (.out(clock_3_out));
  Clock clock_4 (.out(clock_4_out));
  D_Flip_Flop d_ff_2 (
    .clk(not_1_out), .D(and_7_out), .Q(d_ff_2_q), .preset(clock_3_out), .en(1'b1), .reset(or_6_out));  // open: Qn
  or or_1 (or_1_out, d_ff_1_q, d_ff_2_q);
  and and_1 (and_1_out, clock_2_out, or_1_out);
  Clock clock_5 (.out(clock_5_out));
  D_Flip_Flop d_ff_3 (
    .clk(not_1_out), .D(and_8_out), .Q(d_ff_3_q), .preset(clock_4_out), .en(1'b1), .reset(or_5_out));  // open: Qn
  or or_2 (or_2_out, d_ff_4_q, d_ff_3_q);
  and and_2 (and_2_out, clock_2_out, or_2_out);
  not not_3 (not_3_out, d_ff_4_q);
  Counter #(.width(4), .max('hf)) counter_2 (
    .load(not_3_out), .count(1'b1), .Q(counter_2_q), .clk(and_2_out), .clr(and_3_out));  // open: D, carry
  D_Flip_Flop d_ff_4 (
    .clk(not_1_out), .D(and_9_out), .Q(d_ff_4_q), .preset(clock_5_out), .en(1'b1), .reset(or_4_out));  // open: Qn
  and and_3 (and_3_out, and_4_out, clock_7_out);
  and and_4 (and_4_out, undriven, or_3_out);
  or or_3 (or_3_out, d_ff_4_q, d_ff_3_q, d_ff_2_q, d_ff_1_q);
  or or_4 (or_4_out, 1'b0, clock_3_out, clock_4_out, clock_5_out);
  or or_5 (or_5_out, clock_1_out, 1'b0, clock_4_out, clock_5_out);
  or or_6 (or_6_out, clock_1_out, clock_3_out, 1'b0, clock_5_out);
  or or_7 (or_7_out, clock_1_out, clock_3_out, clock_4_out, 1'b0);
  Clock clock_6 (.out(clock_6_out));
  and and_5 (and_5_out, clock_6_out, clock_5_out);
  and and_6 (and_6_out, d_ff_2_q, undriven);
  and and_7 (and_7_out, d_ff_1_q, undriven);
  and and_8 (and_8_out, d_ff_4_q, undriven);
  and and_9 (and_9_out, d_ff_3_q, undriven);
  Clock clock_7 (.out(clock_7_out));
  Counter #(.width(4), .max('hf)) counter_3 (
    .load(1'b0), .count(1'b1), .Q(counter_3_q), .clk(clock_7_out), .clr(and_3_out));  // open: D, carry
  xor xor_1 (xor_1_out, undriven_2, undriven_3);

  // Notes on the sheet:
  //   GAL 22V10
  //   GAL 22V10
  //   74LS273
  //   o4
  //   o3
  //   o2
  //   o1
  //   m7
  //   m6
  //   m5
  //   m4
  //   m3
  //   m2
  //   m1
  //   m0
  //   n2
  //   n1
  //   n0
endmodule
