// Logisim project Logic Diagram 2.circ as structural Verilog: 1 circuit, main circuit main
module main (
);

  wire and_1_out, and_2_out, and_3_out, and_4_out, and_5_out, and_6_out, and_7_out, and_8_out, and_9_out,
       and_10_out, and_11_out, clock_1_out, or_1_out, or_2_out, or_3_out, or_4_out, or_5_out, or_6_out,
       or_7_out, or_8_out, or_9_out, or_10_out, or_11_out, undriven, undriven_2, undriven_3, undriven_4,
       undriven_5, undriven_6, undriven_7, undriven_8, undriven_9, undriven_10, undriven_11, undriven_12,
       undriven_13, undriven_14, undriven_15, undriven_16;

  Clock clock_1 (.out(clock_1_out));
  and and_1 (and_1_out, undriven_2, undriven_3, undriven, undriven_7);
  and and_2 (and_2_out, and_1_out, and_3_out);
  and and_3 (and_3_out, undriven_6, undriven_14, undriven_4, undriven_5);
  or or_1 (or_1_out, undriven_15, undriven_4);
  or or_2 (or_2_out, undriven_10, undriven_14);
  or or_3 (or_3_out, undriven_12, undriven_6);
  or or_4 (or_4_out, undriven_8, undriven_2);
  or or_5 (or_5_out, undriven_13, undriven_3);
  or or_6 (or_6_out, undriven_9, undriven);
  or or_7 (or_7_out, undriven_16, undriven_7);
  or or_8 (or_8_out, undriven_5, undriven_11);
  and and_4 (and_4_out, undriven_2, undriven_8);
  and and_5 (and_5_out, undriven_3, undriven_13);
  and and_6 (and_6_out, undriven, undriven_9);
  and and_7 (and_7_out, undriven_7, undriven_16);
  and and_8 (and_8_out, undriven_5, undriven_5);
  and and_9 (and_9_out, undriven_15, undriven_4);
  and and_10 (and_10_out, undriven_10, undriven_14);
  and and_11 (and_11_out, undriven_12, undriven_6);
  or or_9 (or_9_out, and_4_out, and_5_out, and_6_out, and_7_out);
  or or_10 (or_10_out, and_8_out, and_9_out, and_10_out, and_11_out);
  or or_11 (or_11_out, or_9_out, or_10_out);

  // Notes on the sheet:
  //   TC4503
  //   TC4503
  //   74LS273
  //   HM6116LP-3
  //   n2 n1 n0
  //   GAL22V10
  //   HM6116LP-3
  //   TC4503
  //   TC4503
  //   TC4503
  //   o2
  //   m7
  //   m6
  //   o1
  //   m5
  //   m4
  //   m3
  //   m2
  //   m1
  //   m0
  //   q0
  //   q1
  //   q3
  //   q2
  //   q5
  //   q4
  //   q6
  //   q7
  //   collision
endmodule
