// Logisim project Logic Diagram 3.circ as structural Verilog: 1 circuit, main circuit main
module main (
);

  wire and_1_out, and_2_out, and_3_out, and_4_out, and_5_out, and_6_out, and_7_out, and_8_out, clock_1_out,
       undriven, undriven_2, undriven_3, undriven_4, undriven_5, undriven_6, undriven_7, undriven_8,
       undriven_9, undriven_10, undriven_11, undriven_12, undriven_13, undriven_14, undriven_15, undriven_16,
       undriven_17, undriven_18, undriven_19, undriven_20, undriven_21, undriven_22, undriven_23,
       undriven_24, undriven_25, undriven_26, undriven_27, undriven_28, undriven_29, undriven_30,
       undriven_31, undriven_32, undriven_33, undriven_34, undriven_35, undriven_36, undriven_37,
       undriven_38, undriven_39, undriven_40, undriven_41, undriven_42, undriven_43, undriven_44,
       undriven_45, undriven_46, undriven_47, undriven_48, undriven_49, undriven_50, undriven_51,
       undriven_52, undriven_53, undriven_54, undriven_55, undriven_56, undriven_57, undriven_58,
       undriven_59, undriven_60, undriven_61, undriven_62, undriven_63, undriven_64, undriven_65,
       undriven_66, undriven_67, undriven_68, undriven_69, undriven_70, undriven_71, undriven_72;

  LED led_1 (.in(undriven_9));
  LED led_2 (.in(undriven_10));
  LED led_3 (.in(undriven_11));
  LED led_4 (.in(undriven_12));
  LED led_5 (.in(undriven_13));
  LED led_6 (.in(undriven_14));
  LED led_7 (.in(undriven_15));
  LED led_8 (.in(undriven_16));
  LED led_9 (.in(undriven_17));
  LED led_10 (.in(undriven_18));
  LED led_11 (.in(undriven_19));
  LED led_12 (.in(undriven_20));
  LED led_13 (.in(undriven_21));
  LED led_14 (.in(undriven_22));
  LED led_15 (.in(undriven_23));
  LED led_16 (.in(undriven_24));
  LED led_17 (.in(undriven));
  LED led_18 (.in(undriven_2));
  LED led_19 (.in(undriven_3));
  LED led_20 (.in(undriven_4));
  LED led_21 (.in(undriven_5));
  LED led_22 (.in(undriven_6));
  LED led_23 (.in(undriven_7));
  LED led_24 (.in(undriven_8));
  LED led_25 (.in(undriven_25));
  LED led_26 (.in(undriven_26));
  LED led_27 (.in(undriven_27));
  LED led_28 (.in(undriven_28));
  LED led_29 (.in(undriven_29));
  LED led_30 (.in(undriven_30));
  LED led_31 (.in(undriven_31));
  LED led_32 (.in(undriven_32));
  LED led_33 (.in(undriven_33));
  LED led_34 (.in(undriven_34));
  LED led_35 (.in(undriven_35));
  LED led_36 (.in(undriven_36));
  LED led_37 (.in(undriven_37));
  LED led_38 (.in(undriven_38));
  LED led_39 (.in(undriven_39));
  LED led_40 (.in(undriven_40));
  LED led_41 (.in(undriven_49));
  LED led_42 (.in(undriven_50));
  LED led_43 (.in(undriven_51));
  LED led_44 (.in(undriven_52));
  LED led_45 (.in(undriven_53));
  LED led_46 (.in(undriven_54));
  LED led_47 (.in(undriven_55));
  LED led_48 (.in(undriven_56));
  LED led_49 (.in(undriven_57));
  LED led_50 (.in(undriven_58));
  LED led_51 (.in(undriven_59));
  LED led_52 (.in(undriven_60));
  LED led_53 (.in(undriven_61));
  LED led_54 (.in(undriven_62));
  LED led_55 (.in(undriven_63));
  LED led_56 (.in(undriven_64));
  LED led_57 (.in(undriven_65));
  LED led_58 (.in(undriven_66));
  LED led_59 (.in(undriven_67));
  LED led_60 (.in(undriven_68));
  LED led_61 (.in(undriven_69));
  LED led_62 (.in(undriven_70));
  LED led_63 (.in(undriven_71));
  LED led_64 (.in(undriven_72));
  Clock clock_1 (.out(clock_1_out));
  and and_1 (and_1_out, clock_1_out, undriven_41);
  and and_2 (and_2_out, clock_1_out, undriven_42);
  and and_3 (and_3_out, clock_1_out, undriven_43);
  and and_4 (and_4_out, clock_1_out, undriven_44);
  and and_5 (and_5_out, clock_1_out, undriven_45);
  and and_6 (and_6_out, clock_1_out, undriven_46);
  and and_7 (and_7_out, clock_1_out, undriven_47);
  and and_8 (and_8_out, clock_1_out, undriven_48);

  // Notes on the sheet:
  //   q0
  //   q1
  //   q2
  //   q3
  //   q4
  //   q5
  //   q6
  //   q7
  //   74LS273
  //   74LS273
  //   74LS273
  //   74LS273
  //   74LS273
  //   n0
  //   n1
  //   n2
  //   CD4028
  //   74LS273
  //   74LS273
  //   74LS273
endmodule
